# Fritzing sketch midi_schematic (saved by Fritzing 0.9.0b)
breadboards: 1

parts:
  D7 = Rectifier Diode [part_number=TIP102 package="300 mil [THT]"]
  MIDI_Input1 = DIN-5 jack (MIDI) [package=THT]
  R2 = Resistor [tolerance=±5% resistance=220 package=THT]
  6N139 = IC, DIP package, 8 pins [chip_label=IC]

nets:
  N1: D7.cathode, R2.Pin_1, 6N139.pin2
  N2: D7.anode, MIDI_Input1.4, 6N139.pin3
  N3: MIDI_Input1.5, R2.Pin_0
